// Logisim project circuito.circ as structural Verilog: 4 circuits, main circuit SUMLAT
module SUMLAT (
  input  [7:0] X,
  input  [7:0] Y,
  input  C0,
  output [7:0] out_4
);

  wire b_1_ch, b_1_cl, b_1_ghl, b_1_phl, b_2_ch, b_2_cl, b_2_ghl, b_2_phl, b_3_ch, b_3_cl, b_3_ghl, b_3_phl,
       b_4_ch, b_4_cl, b_5_ch, b_5_cl, b_5_ghl, b_5_phl, b_6_ch, b_6_cl, b_6_ghl, b_6_phl, b_7_ch, b_7_cl,
       b_7_ghl, b_7_phl, fagp_1_gi, fagp_1_pi, fagp_2_gi, fagp_2_pi, fagp_3_gi, fagp_3_pi, fagp_4_gi,
       fagp_4_pi, fagp_5_gi, fagp_5_pi, fagp_6_gi, fagp_6_pi, fagp_7_gi, fagp_7_pi, fagp_8_gi, fagp_8_pi;

  FAGP fagp_1 (.ai(X[7]), .bi(Y[7]), .ci(b_1_ch), .si(out_4[7]), .pi(fagp_1_pi), .gi(fagp_1_gi));  // open: Cout
  B b_1 (
    .PH(fagp_1_pi), .GH(fagp_1_gi), .PL(fagp_2_pi), .GL(fagp_2_gi), .Cin(b_2_ch), .CH(b_1_ch), .CL(b_1_cl),
    .PHL(b_1_phl), .GHL(b_1_ghl));
  FAGP fagp_2 (.ai(X[6]), .bi(Y[6]), .ci(b_1_cl), .si(out_4[6]), .pi(fagp_2_pi), .gi(fagp_2_gi));  // open: Cout
  B b_2 (
    .PH(b_1_phl), .GH(b_1_ghl), .PL(b_3_phl), .GL(b_3_ghl), .Cin(b_4_ch), .CH(b_2_ch), .CL(b_2_cl),
    .PHL(b_2_phl), .GHL(b_2_ghl));
  FAGP fagp_3 (.ai(X[5]), .bi(Y[5]), .ci(b_3_ch), .si(out_4[5]), .pi(fagp_3_pi), .gi(fagp_3_gi));  // open: Cout
  B b_3 (
    .PH(fagp_3_pi), .GH(fagp_3_gi), .PL(fagp_4_pi), .GL(fagp_4_gi), .Cin(b_2_cl), .CH(b_3_ch), .CL(b_3_cl),
    .PHL(b_3_phl), .GHL(b_3_ghl));
  FAGP fagp_4 (.ai(X[4]), .bi(Y[4]), .ci(b_3_cl), .si(out_4[4]), .pi(fagp_4_pi), .gi(fagp_4_gi));  // open: Cout
  B b_4 (.PH(b_2_phl), .GH(b_2_ghl), .PL(b_6_phl), .GL(b_6_ghl), .Cin(C0), .CH(b_4_ch), .CL(b_4_cl));  // open: PHL, GHL
  FAGP fagp_5 (.ai(X[3]), .bi(Y[3]), .ci(b_5_ch), .si(out_4[3]), .pi(fagp_5_pi), .gi(fagp_5_gi));  // open: Cout
  B b_5 (
    .PH(fagp_5_pi), .GH(fagp_5_gi), .PL(fagp_6_pi), .GL(fagp_6_gi), .Cin(b_6_ch), .CH(b_5_ch), .CL(b_5_cl),
    .PHL(b_5_phl), .GHL(b_5_ghl));
  FAGP fagp_6 (.ai(X[2]), .bi(Y[2]), .ci(b_5_cl), .si(out_4[2]), .pi(fagp_6_pi), .gi(fagp_6_gi));  // open: Cout
  B b_6 (
    .PH(b_5_phl), .GH(b_5_ghl), .PL(b_7_phl), .GL(b_7_ghl), .Cin(b_4_cl), .CH(b_6_ch), .CL(b_6_cl),
    .PHL(b_6_phl), .GHL(b_6_ghl));
  FAGP fagp_7 (.ai(X[1]), .bi(Y[1]), .ci(b_7_ch), .si(out_4[1]), .pi(fagp_7_pi), .gi(fagp_7_gi));  // open: Cout
  B b_7 (
    .PH(fagp_7_pi), .GH(fagp_7_gi), .PL(fagp_8_pi), .GL(fagp_8_gi), .Cin(b_6_cl), .CH(b_7_ch), .CL(b_7_cl),
    .PHL(b_7_phl), .GHL(b_7_ghl));
  FAGP fagp_8 (.ai(X[0]), .bi(Y[0]), .ci(b_7_cl), .si(out_4[0]), .pi(fagp_8_pi), .gi(fagp_8_gi));  // open: Cout
endmodule

// Full Adder
module FAGP (
  input  ai,
  input  bi,
  input  ci,
  output si,
  output pi,
  output gi,
  output Cout
);

  wire and_2_out, and_3_out, or_2_out, xor_1_out;

  or or_1 (pi, ai, bi);
  and and_1 (gi, ai, bi);
  or or_2 (or_2_out, ai, bi);
  xor xor_1 (xor_1_out, ai, bi);
  xor xor_2 (si, xor_1_out, ci);
  and and_2 (and_2_out, ci, or_2_out);
  and and_3 (and_3_out, bi, ai);
  or or_3 (Cout, and_2_out, and_3_out);
endmodule

// Bloque B
module B (
  input  PH,
  input  GH,
  input  PL,
  input  GL,
  input  Cin,
  output CH,
  output CL,
  output PHL,
  output GHL
);

  wire and_1_out, and_2_out;

  and and_1 (and_1_out, PH, GL);
  and and_2 (and_2_out, PL, Cin);
  and and_3 (PHL, PH, PL);
  or or_1 (GHL, GH, and_1_out);
  or or_2 (CH, GL, and_2_out);

  assign CL = Cin;
endmodule

module test (
  input  [7:0] in_1,
  input  [7:0] in_2,
  input  in_3,
  output [7:0] out_4
);

  SUMLAT sumlat_1 (.X(in_1), .Y(in_2), .C0(in_3), .out_4(out_4));
endmodule
