// Logisim project Modo_Alternativo.circ as structural Verilog: 1 circuit, main circuit ModoAlternativo
module ModoAlternativo (
  input  Z1,
  input  Z2,
  input  Z3,
  input  Z4,
  input  A,
  input  B,
  input  C,
  input  D,
  input  E,
  output ModoAlt
);

  wire and_1_out, and_2_out, and_3_out, and_4_out, and_5_out, and_6_out, and_7_out, and_8_out, and_9_out,
       and_10_out, and_11_out, and_12_out, and_13_out, not_1_out, not_2_out, not_3_out, not_4_out, not_5_out,
       not_6_out, not_7_out, not_8_out, not_9_out, not_10_out, not_11_out, or_1_out, or_2_out;

  not not_1 (not_1_out, A);
  not not_2 (not_2_out, B);
  not not_3 (not_3_out, C);
  not not_4 (not_4_out, D);
  not not_5 (not_5_out, E);
  not not_6 (not_6_out, Z1);
  not not_7 (not_7_out, Z2);
  not not_8 (not_8_out, Z3);
  not not_9 (not_9_out, Z4);
  not not_10 (not_10_out, Z3);
  not not_11 (not_11_out, Z2);
  and and_1 (and_1_out, not_2_out, D, not_5_out);
  and and_2 (and_2_out, not_1_out, B, not_3_out, E);
  and and_3 (and_3_out, B, C, not_4_out, not_5_out);
  and and_4 (and_4_out, not_2_out, not_4_out, E);
  and and_5 (and_5_out, A, B, C, D, E);
  and and_6 (and_6_out, A, B, not_3_out, not_4_out);
  and and_7 (and_7_out, A, B, not_3_out, not_5_out);
  and and_8 (and_8_out, not_1_out, not_2_out, C, E);
  and and_9 (and_9_out, A, not_2_out, not_3_out, E);
  and and_10 (and_10_out, not_7_out, not_8_out, not_9_out);
  and and_11 (and_11_out, not_6_out, Z2, not_10_out, Z4);
  and and_12 (and_12_out, Z1, not_11_out, Z4);
  and and_13 (and_13_out, Z1, Z3, Z4);
  or or_1 (or_1_out, and_1_out, and_2_out, and_3_out, and_4_out, and_5_out, and_6_out, and_7_out, and_8_out, and_9_out);
  or or_2 (or_2_out, and_10_out, and_11_out, and_12_out, and_13_out);
  and and_14 (ModoAlt, or_2_out, or_1_out);
endmodule
