// Logisim project circuito_etapa2.circ as structural Verilog: 7 circuits, main circuit SUMLAT
module Controlador (
  input  Z4,
  input  Z3,
  input  Z2,
  input  Z1,
  input  A,
  input  B,
  input  C,
  input  D,
  input  E,
  input  Iniciar,
  output [7:0] out_11
);

  wire and_1_out, and_2_out, and_3_out, clock_1_out, modoalterna_1_modoalternativo, not_1_out, not_2_out,
       not_3_out, not_4_out, not_5_out, or_1_out, or_2_out;
  wire [7:0] multiplexer_1_out, sumlat_1_s;

  or or_1 (or_1_out, Iniciar, and_2_out);
  Multiplexer #(.width(8)) multiplexer_1 (.in0(sumlat_1_s), .in1(8'h30), .out(multiplexer_1_out), .sel(or_1_out));
  Clock clock_1 (.out(clock_1_out));
  SUMLAT sumlat_1 (.X(8'h3), .Y(out_11), .S(sumlat_1_s));  // open: C0, Overflow
  Counter #(.ongoal("stay")) counter_1 (
    .load(or_2_out), .up(1'b1), .clk(clock_1_out), .D(multiplexer_1_out), .Q(out_11));  // open: clr, count, carry
  or or_2 (or_2_out, and_1_out, and_3_out, and_2_out, Iniciar);
  modoalterna modoalterna_1 (
    .Z4(Z4), .Z3(Z3), .Z2(Z2), .Z1(Z1), .A(A), .B(B), .C(C), .D(D), .E(E),
    .ModoAlternativo(modoalterna_1_modoalternativo));
  not not_1 (not_1_out, out_11[1]);
  not not_2 (not_2_out, out_11[0]);
  and and_1 (and_1_out, out_11[2], not_1_out, not_2_out);
  and and_2 (and_2_out, out_11[2], out_11[1], out_11[0]);
  not not_3 (not_3_out, out_11[0]);
  not not_4 (not_4_out, out_11[1]);
  not not_5 (not_5_out, out_11[2]);
  and and_3 (and_3_out, not_5_out, not_4_out, not_3_out, modoalterna_1_modoalternativo);

  // Notes on the sheet:
  //   Estado + 3
  //   Estado Actual
endmodule

module SUMLAT (
  input  [7:0] X,
  input  [7:0] Y,
  input  C0,
  output Overflow,
  output [7:0] S
);

  wire b_1_cl, b_1_ghl, b_1_phl, b_2_ch, b_2_cl, b_2_ghl, b_2_phl, b_3_ch, b_3_cl, b_3_ghl, b_3_phl, b_4_ch,
       b_4_cl, b_5_ch, b_5_cl, b_5_ghl, b_5_phl, b_6_ch, b_6_cl, b_6_ghl, b_6_phl, b_7_ch, b_7_cl, b_7_ghl,
       b_7_phl, fagp_1_p3, fagp_1_p5, fagp_1_p6, fagp_2_gi, fagp_2_pi, fagp_3_gi, fagp_3_pi, fagp_4_gi,
       fagp_4_pi, fagp_5_gi, fagp_5_pi, fagp_6_gi, fagp_6_pi, fagp_7_gi, fagp_7_pi, fagp_8_gi, fagp_8_pi;

  // FAGP fagp_1: pin names not known; wires that end beside it: X[7], Y[7], fagp_1_p3, S[7], fagp_1_p5, fagp_1_p6, Overflow
  B b_1 (
    .PH(fagp_1_p5), .GH(fagp_1_p6), .PL(fagp_2_pi), .GL(fagp_2_gi), .Cin(b_2_ch), .CH(fagp_1_p3),
    .CL(b_1_cl), .PHL(b_1_phl), .GHL(b_1_ghl));
  FAGP fagp_2 (.ai(X[6]), .bi(Y[6]), .ci(b_1_cl), .si(S[6]), .pi(fagp_2_pi), .gi(fagp_2_gi));  // open: Cout
  B b_2 (
    .PH(b_1_phl), .GH(b_1_ghl), .PL(b_3_phl), .GL(b_3_ghl), .Cin(b_4_ch), .CH(b_2_ch), .CL(b_2_cl),
    .PHL(b_2_phl), .GHL(b_2_ghl));
  FAGP fagp_3 (.ai(X[5]), .bi(Y[5]), .ci(b_3_ch), .si(S[5]), .pi(fagp_3_pi), .gi(fagp_3_gi));  // open: Cout
  B b_3 (
    .PH(fagp_3_pi), .GH(fagp_3_gi), .PL(fagp_4_pi), .GL(fagp_4_gi), .Cin(b_2_cl), .CH(b_3_ch), .CL(b_3_cl),
    .PHL(b_3_phl), .GHL(b_3_ghl));
  FAGP fagp_4 (.ai(X[4]), .bi(Y[4]), .ci(b_3_cl), .si(S[4]), .pi(fagp_4_pi), .gi(fagp_4_gi));  // open: Cout
  B b_4 (.PH(b_2_phl), .GH(b_2_ghl), .PL(b_6_phl), .GL(b_6_ghl), .Cin(C0), .CH(b_4_ch), .CL(b_4_cl));  // open: PHL, GHL
  FAGP fagp_5 (.ai(X[3]), .bi(Y[3]), .ci(b_5_ch), .si(S[3]), .pi(fagp_5_pi), .gi(fagp_5_gi));  // open: Cout
  B b_5 (
    .PH(fagp_5_pi), .GH(fagp_5_gi), .PL(fagp_6_pi), .GL(fagp_6_gi), .Cin(b_6_ch), .CH(b_5_ch), .CL(b_5_cl),
    .PHL(b_5_phl), .GHL(b_5_ghl));
  FAGP fagp_6 (.ai(X[2]), .bi(Y[2]), .ci(b_5_cl), .si(S[2]), .pi(fagp_6_pi), .gi(fagp_6_gi));  // open: Cout
  B b_6 (
    .PH(b_5_phl), .GH(b_5_ghl), .PL(b_7_phl), .GL(b_7_ghl), .Cin(b_4_cl), .CH(b_6_ch), .CL(b_6_cl),
    .PHL(b_6_phl), .GHL(b_6_ghl));
  FAGP fagp_7 (.ai(X[1]), .bi(Y[1]), .ci(b_7_ch), .si(S[1]), .pi(fagp_7_pi), .gi(fagp_7_gi));  // open: Cout
  B b_7 (
    .PH(fagp_7_pi), .GH(fagp_7_gi), .PL(fagp_8_pi), .GL(fagp_8_gi), .Cin(b_6_cl), .CH(b_7_ch), .CL(b_7_cl),
    .PHL(b_7_phl), .GHL(b_7_ghl));
  FAGP fagp_8 (.ai(X[0]), .bi(Y[0]), .ci(b_7_cl), .si(S[0]), .pi(fagp_8_pi), .gi(fagp_8_gi));  // open: Cout
endmodule

// Full Adder
module FAGP (
  input  ai,
  input  bi,
  input  ci,
  output si,
  output pi,
  output gi,
  output Cout
);

  wire and_2_out, xor_1_out;

  or or_1 (pi, ai, bi);
  and and_1 (gi, ai, bi);
  xor xor_1 (xor_1_out, ai, bi);
  xor xor_2 (si, xor_1_out, ci);
  and and_2 (and_2_out, pi, ci);
  or or_2 (Cout, gi, and_2_out);
endmodule

// Bloque B
module B (
  input  PH,
  input  GH,
  input  PL,
  input  GL,
  input  Cin,
  output CH,
  output CL,
  output PHL,
  output GHL
);

  wire and_1_out, and_2_out;

  and and_1 (and_1_out, PH, GL);
  and and_2 (and_2_out, PL, Cin);
  and and_3 (PHL, PH, PL);
  or or_1 (GHL, GH, and_1_out);
  or or_2 (CH, GL, and_2_out);

  assign CL = Cin;
endmodule

module modoalterna (
  input  Z4,
  input  Z3,
  input  Z2,
  input  Z1,
  input  A,
  input  B,
  input  C,
  input  D,
  input  E,
  output ModoAlternativo
);

  wire f1_1_s, f2_1_s;

  f1 f1_1 (.Z4(Z4), .Z3(Z3), .Z2(Z2), .Z1(Z1), .S(f1_1_s));
  f2 f2_1 (.A(A), .B(B), .C(C), .D(D), .E(E), .S(f2_1_s));
  and and_1 (ModoAlternativo, f1_1_s, f2_1_s);
endmodule

module f1 (
  input  Z4,
  input  Z3,
  input  Z2,
  input  Z1,
  output S
);

  ROM #(.addrWidth(4), .dataWidth(1)) rom_1 (.addr({Z1, Z2, Z3, Z4}));  // open: data

  // Notes on the sheet:
  //   contents of rom_1 (hex, n*v repeats v):
  //   1 4*0 1 0 0 1 1 0 1 0 0 0 1
endmodule

module f2 (
  input  A,
  input  B,
  input  C,
  input  D,
  input  E,
  output S
);

  wire and_1_out, and_2_out, and_3_out, and_4_out, and_5_out, and_6_out, and_7_out, and_8_out, and_9_out,
       not_1_out, not_2_out, not_3_out, not_4_out, not_5_out;

  not not_1 (not_1_out, A);
  not not_2 (not_2_out, B);
  not not_3 (not_3_out, C);
  not not_4 (not_4_out, D);
  not not_5 (not_5_out, E);
  and and_1 (and_1_out, not_2_out, D, not_5_out);
  and and_2 (and_2_out, not_1_out, B, not_3_out, E);
  and and_3 (and_3_out, B, C, not_4_out, not_5_out);
  and and_4 (and_4_out, not_2_out, not_4_out, E);
  and and_5 (and_5_out, A, B, C, D, E);
  and and_6 (and_6_out, A, B, not_3_out, not_4_out);
  and and_7 (and_7_out, A, B, not_3_out, not_5_out);
  and and_8 (and_8_out, not_1_out, not_2_out, C, E);
  and and_9 (and_9_out, A, not_2_out, not_3_out, E);
  or or_1 (S, and_1_out, and_2_out, and_3_out, and_4_out, and_5_out, and_6_out, and_7_out, and_8_out, and_9_out);
endmodule
